# Fritzing sketch fritizing-RGB-LED (saved by Fritzing 0.9.1b)
circuit board: 8.46667cm x 5.64444cm
breadboards: 1

parts:
  Part1 = Arduino Uno (Rev3)
  LED1 = RGB LED (com. cathode, rgb) [package="5 mm [THT]"]
  R1 = Resistor [tolerance=±5% resistance=220 package=THT]
  R2 = Resistor [tolerance=±5% resistance=220 package=THT]
  R3 = Resistor [tolerance=±5% resistance=220 package=THT]

nets:
  N1: Part1.GND, LED1.common_cathode
  N2: Part1.D5_PWM, R3.Pin_0
  N3: Part1.D6_PWM, R2.Pin_0
  N4: Part1.D7, R1.Pin_0
  N5: LED1.red_anode, R1.Pin_1
  N6: LED1.green_anode, R2.Pin_1
  N7: LED1.blue_anode, R3.Pin_1

// code stored in the sketch: Fritizing-RGB-LED-arduino.ino
int red = 5;
int green = 6;
int blue = 7;


void setup() {
	pinMode(red, OUTPUT);
	pinMode(blue, OUTPUT);
	pinMode(green, OUTPUT);


	digitalWrite(red, LOW);
	digitalWrite(blue, LOW);
	digitalWrite(green, LOW);
}


void loop() {
	digitalWrite(red, HIGH); // RED
	delay(1000);
	digitalWrite(blue, HIGH); // PURPLE
	delay(1000);
	digitalWrite(green, HIGH); // WHITE
	delay(1000);
	digitalWrite(red, LOW); // YELLOW
	delay(1000);
	digitalWrite(green, LOW); // BLUE
	delay(1000);
	digitalWrite(blue, LOW); // blank
} // End loop
